# Fritzing sketch mando (saved by Fritzing 0.9.3b)
breadboards: 1

parts:
  U1 = ESP32S-HiLetgo [part_number=ESP32S-HiLetgo]
  Componente1 = Thumb Joystick
  Componente2 = Thumb Joystick
  R1 = Resistor [tolerance=±5% resistance=220 package=THT]
  LED1 = LED - 5mm [color="Green (565nm)" package="5 mm [THT]"]
  LED3 = LED - 5mm [color="Red (633nm)" package="5 mm [THT]"]
  U2 = Mini-360 DC-DC Buck converter [package=THT]
  R2 = Resistor [tolerance=±5% resistance=220 package=THT]
  VCC1 = Battery block 9V  # not connected

nets:
  VCC: U1.3.3, Componente1.VCC, Componente2.VCC
  N1: U1.GPIO39, Componente2.VERT
  N2: U1.GPIO34, Componente2.HORZ
  N3: U1.GPIO32, Componente1.VERT
  N4: U1.GPIO33, Componente1.HORZ
  GND: U1.GND, Componente1.GND, Componente2.GND, LED1.cathode, LED3.anode, U2.OUT-
  N5: U1.VIN, U2.OUT+
  N6: U1.GPIO16, Componente2.SEL
  N7: U1.GPIO17, Componente1.SEL
  N8: U1.GPIO5, R1.Pin_1
  N9: U1.GPIO18, R2.Pin_1
  N10: R1.Pin_0, LED3.cathode
  N11: LED1.anode, R2.Pin_0

custom parts:
  ESP32S-HiLetgo: HiLetgo ESP-WROOM-32 ESP32 ESP-32S Development Board 2.4GHz Dual-Mode WiFi + Bluetooth Dual Cores Microcontroller The ESP32 integrated with Antenna switches, RF Balun, power amplifiers, low-noise amplifiers, filters, and management modules, and the entire solution occupies the least area of PCB. 2.4 GHz Wi-Fi plus Bluetooth dual-mode chip, with TSMC Ultra-low power consumption 40nm technology,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
  Mini-360 DC-DC Buck converter: Mini-360 DC-DC Buck converter. Tiny buck step down voltage converter, input voltage 4.75 to 23V output 1 to 17V adjustable. Available from ebay and the like.
